# Fritzing sketch emotIOn (saved by Fritzing 0.9.3b)
circuit board: 8.46667cm x 5.64444cm

parts:
  Part1 = MicroSD Card Module
  Part2 = NeoPixel Stick [part_number=1426]
  U1 = NodeMCU V3.0
  U2 = POT [package=pot_mammoth]
  VCC1 = Battery

nets:
  N1: Part1.VCC, VCC1.+
  N2: Part1.MISO, U1.D6
  N3: Part1.MOSI, U1.D7
  N4: Part1.SCK, U1.D5
  N5: Part1.CS, U1.D2
  N6: Part2.DATAIN, U1.D8
  N7: U1.GND, VCC1.-
  N8: U1.A0, U2.A

notes:
  5V Battery - Power Supply
  Adafruit Ring With 8 LEDS
  1KOhm Potentiometer
  SD Card Reader Pin Label Order
  CS - SCK - MOSI - MISO - VCC - GND

custom parts:
  NeoPixel Stick: Make your own little LED strip arrangement with this stick of NeoPixel LEDs. We crammed 8 of the tiny 5050 (5mm x 5mm) smart RGB LEDs onto a PCB with mounting holes and a chainable design. Use only one microcontroller pin to control as many as you can chain together! Each LED is addressable as the driver chip is inside the LED. Each one has ~18mA constant current drive so the color will be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
  NodeMCU V3.0: ESP8266 based NodeMCU
